// Logisim project MiniALU.circ as structural Verilog: 1 circuit, main circuit main
module main (
);

  wire adder_2_cout, AddOp, and_1_out, and_2_out, and_3_out, clock, comparator_1_eq, comparator_1_gt,
       comparator_1_lt, d_ff_1_q, d_ff_1_qn, d_ff_2_q, d_ff_2_qn, d_ff_3_q, d_ff_3_qn, decoder_1_out1,
       decoder_1_out2, demultiplexer_2_out4, demultiplexer_2_out6, demultiplexer_2_out7,
       demultiplexer_2_out8, EqOp, GTOp, LTOp, NEQOp, or_3_out, or_5_out, or_6_out, SubOp, xor_1_out;
  wire [2:0] adder_1_out, RPC_q;
  wire [3:0] ALUResult_q, ALUResult_q_2, OpcodeHB, OpcodeLB;
  wire [7:0] addResult, and_4_out, and_5_out, bit_extender_1_out, compResult, or_4_out, ValB, ValC,
       willDisplayAdd, willDisplayComp, xor_2_out;
  wire [23:16] rom_1_data;

  Clock clock_1 (.out(clock));
  D_Flip_Flop d_ff_1 (.D(d_ff_1_qn), .clk(clock), .Q(d_ff_1_q), .Qn(d_ff_1_qn));  // open: preset, reset
  D_Flip_Flop d_ff_2 (.D(d_ff_2_qn), .clk(d_ff_1_qn), .Q(d_ff_2_q), .Qn(d_ff_2_qn));  // open: preset, reset
  D_Flip_Flop d_ff_3 (.D(d_ff_3_qn), .clk(d_ff_2_qn), .Q(d_ff_3_q), .Qn(d_ff_3_qn));  // open: preset, reset
  ROM #(.addrWidth(3), .dataWidth(32)) rom_1 (.addr(RPC_q), .data({OpcodeHB, OpcodeLB, rom_1_data, ValB, ValC}));
  Register #(.width(3)) RPC (.D(adder_1_out), .en(1'b1), .Q(RPC_q), .clk(clock));  // open: clr
  Decoder #(.enable("false"), .select(4)) decoder_1 (
    .out1(decoder_1_out1), .out2(decoder_1_out2), .sel(OpcodeHB));  // open: out0, out3, out4, out5, out6, out7, out8, out9, out10, out11, out12, out13, out14, out15
  Adder #(.width(3)) adder_1 (.a(3'b001), .b(RPC_q), .out(adder_1_out));  // open: cin, cout
  Demultiplexer #(.select(4)) demultiplexer_1 (
    .out0(AddOp), .out1(SubOp), .in(decoder_1_out1), .sel(OpcodeLB));  // open: out2, out3, out4, out5, out6, out7, out8, out9, out10, out11, out12, out13, out14, out15
  Demultiplexer #(.select(4)) demultiplexer_2 (
    .out4(demultiplexer_2_out4), .out5(NEQOp), .out6(demultiplexer_2_out6), .out7(demultiplexer_2_out7),
    .out8(demultiplexer_2_out8), .out9(LTOp), .in(decoder_1_out2), .sel(OpcodeLB));  // open: out0, out1, out2, out3, out10, out11, out12, out13, out14, out15
  or or_1 (EqOp, demultiplexer_2_out4, NEQOp, demultiplexer_2_out6, demultiplexer_2_out7);
  or or_2 (GTOp, demultiplexer_2_out6, demultiplexer_2_out8);
  and and_1 (and_1_out, GTOp, comparator_1_gt);
  Comparator comparator_1 (.a(ValB), .b(ValC), .gt(comparator_1_gt), .eq(comparator_1_eq), .lt(comparator_1_lt));
  and and_2 (and_2_out, comparator_1_lt, LTOp);
  assign bit_extender_1_out = {{7{SubOp}}, SubOp};  // Bit_Extender bit_extender_1
  xor xor_1 (xor_1_out, NEQOp, comparator_1_eq);
  Adder adder_2 (.a(ValB), .b(xor_2_out), .out(addResult), .cin(SubOp), .cout(adder_2_cout));
  assign xor_2_out = ValC ^ bit_extender_1_out;  // XOR_Gate xor_2, 8 bits wide
  LED CarryOut (.in(adder_2_cout));
  and and_3 (and_3_out, EqOp, xor_1_out);
  or or_3 (or_3_out, and_1_out, and_3_out, and_2_out);
  assign compResult = {{7{or_3_out}}, or_3_out};  // Bit_Extender bit_extender_2
  Hex_Digit_Display hex_digit_display_1 (.value(ALUResult_q_2));  // open: dp
  assign or_4_out = and_4_out | and_5_out;  // OR_Gate or_4, 8 bits wide
  assign and_4_out = compResult & willDisplayComp;  // AND_Gate and_4, 8 bits wide
  assign and_5_out = addResult & willDisplayAdd;  // AND_Gate and_5, 8 bits wide
  assign willDisplayAdd = {{7{or_5_out}}, or_5_out};  // Bit_Extender bit_extender_3
  or or_5 (or_5_out, SubOp, AddOp);
  assign willDisplayComp = {{7{or_6_out}}, or_6_out};  // Bit_Extender bit_extender_4
  or or_6 (or_6_out, EqOp, NEQOp, GTOp, LTOp);
  Hex_Digit_Display hex_digit_display_2 (.value(ALUResult_q));  // open: dp
  Register ALUResult (.D(or_4_out), .Q({ALUResult_q_2, ALUResult_q}), .clk(clock));  // open: en, clr

  // Notes on the sheet:
  //   contents of rom_1 (hex, n*v repeats v):
  //   10ff0102 11ff0803 10ffff01 24ff4a4a 28ff0201 24ff00ff 28ff0102 26ff0301
endmodule
